// Logisim project P1-aux1.circ as structural Verilog: 9 circuits, main circuit num
module num (
  input  x3,
  input  x2,
  input  x1,
  input  x0,
  output a,
  output f,
  output b,
  output g,
  output e,
  output c,
  output d
);

  a u_A (.x3(x3), .x2(x2), .x1(x1), .x0(x0), .a(a));
  b u_B (.x3(x3), .x2(x2), .x1(x1), .x0(x0), .b(b));
  c u_C (.x3(x3), .x2(x2), .x1(x1), .x0(x0), .c(c));
  d u_D (.x3(x3), .x2(x2), .x1(x1), .x0(x0), .d(d));
  e u_E (.x3(x3), .x2(x2), .x1(x1), .x0(x0), .e(e));
  f u_F (.x3(x3), .x2(x2), .x1(x1), .x0(x0), .f(f));
  g u_G (.x3(x3), .x2(x2), .x1(x1), .x0(x0), .g(g));
endmodule

module a (
  input  x3,
  input  x2,
  input  x1,
  input  x0,
  output a
);

  wire and_1_out, and_2_out, not_1_out, not_2_out;

  not not_1 (not_1_out, x0);
  not not_2 (not_2_out, x2);
  and and_1 (and_1_out, not_1_out, not_2_out);
  and and_2 (and_2_out, x2, x0);
  or or_1 (a, x3, x1, and_1_out, and_2_out);
endmodule

module b (
  input  x3,
  input  x2,
  input  x1,
  input  x0,
  output b
);

  wire and_1_out, and_2_out, not_1_out, not_2_out, not_3_out;

  not not_1 (not_1_out, x2);
  not not_2 (not_2_out, x1);
  not not_3 (not_3_out, x0);
  and and_1 (and_1_out, not_2_out, not_3_out);
  and and_2 (and_2_out, x1, x0);
  or or_1 (b, not_1_out, and_1_out, and_2_out);
endmodule

module c (
  input  x3,
  input  x2,
  input  x1,
  input  x0,
  output c
);

  wire not_1_out;

  not not_1 (not_1_out, x1);
  or or_1 (c, x2, not_1_out, x0);
endmodule

module d (
  input  x3,
  input  x2,
  input  x1,
  input  x0,
  output d
);

  wire and_1_out, and_2_out, and_3_out, and_4_out, not_1_out, not_2_out, not_3_out;

  not not_1 (not_1_out, x0);
  not not_2 (not_2_out, x2);
  not not_3 (not_3_out, x1);
  and and_1 (and_1_out, not_2_out, not_1_out);
  and and_2 (and_2_out, x2, not_3_out, x0);
  and and_3 (and_3_out, x1, not_1_out);
  and and_4 (and_4_out, not_2_out, x1);
  or or_1 (d, x3, and_2_out, and_3_out, and_4_out, and_1_out);
endmodule

module e (
  input  x3,
  input  x2,
  input  x1,
  input  x0,
  output e
);

  wire and_1_out, and_2_out, not_1_out, not_2_out;

  not not_1 (not_1_out, x2);
  not not_2 (not_2_out, x0);
  and and_1 (and_1_out, not_1_out, not_2_out);
  and and_2 (and_2_out, x1, not_2_out);
  or or_1 (e, and_1_out, and_2_out);
endmodule

module f (
  input  x3,
  input  x2,
  input  x1,
  input  x0,
  output f
);

  wire and_1_out, and_2_out, and_3_out, not_1_out, not_2_out;

  not not_1 (not_1_out, x1);
  not not_2 (not_2_out, x0);
  and and_1 (and_1_out, x2, not_1_out);
  and and_2 (and_2_out, x2, not_2_out);
  and and_3 (and_3_out, not_1_out, not_2_out);
  or or_1 (f, x3, and_1_out, and_2_out, and_3_out);
endmodule

module g (
  input  x3,
  input  x2,
  input  x1,
  input  x0,
  output g
);

  wire and_1_out, and_2_out, and_3_out, not_1_out, not_2_out, not_3_out;

  not not_1 (not_1_out, x0);
  not not_2 (not_2_out, x1);
  not not_3 (not_3_out, x2);
  and and_1 (and_1_out, x1, not_1_out);
  and and_2 (and_2_out, x2, not_2_out);
  and and_3 (and_3_out, not_3_out, x1);
  or or_1 (g, x3, and_1_out, and_2_out, and_3_out);
endmodule

module digital (
  input  x3,
  input  x2,
  input  x1,
  input  x0
);

  wire num_1_a, num_1_b, num_1_c, num_1_d, num_1_e, num_1_f, num_1_g;

  num num_1 (
    .x3(x3), .x2(x2), .x1(x1), .x0(x0), .b(num_1_b), .g(num_1_g), .c(num_1_c), .d(num_1_d), .a(num_1_a),
    .f(num_1_f), .e(num_1_e));
  _7_Segment_Display u_7_segment_display_1 (
    .g(num_1_g), .f(num_1_f), .a(num_1_a), .b(num_1_b), .e(num_1_e), .d(num_1_d), .c(num_1_c));  // open: dp
endmodule
